# Fritzing sketch helmet_rgb_breath_led (saved by Fritzing 0.9.3b)
breadboards: 1

parts:
  U1 = Battery Holders [package=battery-aa-kit]
  U3 = ATTINY45 [package=dip]
  R1 = Resistor [tolerance=±5% resistance=1.2k package="0402 [SMD]"]
  OLED1 = OLED 128x64 I2C Monochrome Display GND-VDD
  U4 = WS2812 RGB LED matrix 1x8
  元件1 = Voltmeter
  C1 = Electrolytic Capacitor [capacitance=1µF package="100 mil [THT, electrolytic]"]

nets:
  VCC: U1.+, U3.VCC, OLED1.VDD, U4.VCC, 元件1.Vss, 元件1.Vcc, C1.+
  GND: U1.-, U3.GND, OLED1.GND, U4.GND, 元件1.GND, C1.-
  N1: U3.PB0(MOSI), OLED1.SDA
  N2: U3.PB1(MISO), R1.Pin_0
  N3: U3.PB2(SCK_ADC1), OLED1.SCK
  N4: R1.Pin_1, U4.DIN

notes:
  14500 800mAh 3.7V
  ATTiny85
  1.2KΩ
  W2812B 1x15
  Volt meter
  OLED 128x64
  安全帽呼吸燈 - 開發板
  羽山秋人 https://3wa.tw
  2024-07-07
  100㎌ 10V

custom parts:
  OLED 128x64 I2C Monochrome Display GND-VDD: OLED 128x64 I2C Monochrome Display. Note: there are two variants of this part, this one is the GND VDD SCK SDA variant. The other is VDD GND SCK SDA. Make sure you select the part that matches your module as using the incorrect part will probably destroy your module! In addition the mounting holes are marked on silkscreen but not by default drilled. If you want drilled mounting holes, copy a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
  WS2812 RGB LED matrix 1x8: WS2812 matrix 1x8
